// Logisim project alu_registry.circ as structural Verilog
module alu_registry (
  input  [7:0] C,
  input  [2:0] slctC,
  input  [2:0] slctB,
  input  [2:0] slctA,
  input  [3:0] slctOP,
  output [7:0] out_6,
  output out_7
);

  wire decoder_1_out0, decoder_1_out1, decoder_1_out2, decoder_1_out3, decoder_1_out4, decoder_1_out5,
       decoder_1_out6, decoder_1_out7;
  wire [7:0] multiplexer_1_out, multiplexer_2_out, registry_1_s0, registry_1_s1, registry_1_s2,
       registry_1_s3, registry_1_s4, registry_1_s5, registry_1_s6, registry_1_s7_8bit;

  Decoder #(.select(3)) decoder_1 (
    .out0(decoder_1_out0), .out1(decoder_1_out1), .out2(decoder_1_out2), .out3(decoder_1_out3),
    .out4(decoder_1_out4), .out5(decoder_1_out5), .out6(decoder_1_out6), .out7(decoder_1_out7), .sel(slctC),
    .en(1'b1));
  registry registry_1 (
    .C(C), .R0(decoder_1_out0), .R1(decoder_1_out1), .R2(decoder_1_out2), .R3(decoder_1_out3),
    .R4(decoder_1_out4), .R5(decoder_1_out5), .R6(decoder_1_out6), .R7(decoder_1_out7), .S0(registry_1_s0),
    .S1(registry_1_s1), .S2(registry_1_s2), .S3(registry_1_s3), .S4(registry_1_s4), .S5(registry_1_s5),
    .S6(registry_1_s6), .S7_8bit(registry_1_s7_8bit), .S7_1bit(out_7));
  Multiplexer #(.select(3), .width(8)) multiplexer_1 (
    .in0(registry_1_s0), .in1(registry_1_s1), .in2(registry_1_s2), .in3(registry_1_s3), .in4(registry_1_s4),
    .in5(registry_1_s5), .in6(registry_1_s6), .in7(registry_1_s7_8bit), .out(multiplexer_1_out), .sel(slctB));
  Multiplexer #(.select(3), .width(8)) multiplexer_2 (
    .in0(registry_1_s0), .in1(registry_1_s1), .in2(registry_1_s2), .in3(registry_1_s3), .in4(registry_1_s4),
    .in5(registry_1_s5), .in6(registry_1_s6), .in7(registry_1_s7_8bit), .out(multiplexer_2_out), .sel(slctA));
  ALU alu_1 (.A(multiplexer_2_out), .B(multiplexer_1_out), .slct(slctOP), .S(out_6));  // open: Err
endmodule
