// Logisim project cpu_ram.circ as structural Verilog: 2 circuits, main circuit ram_data
module ram_data (
  input  [7:0] stor_in,
  input  [7:0] stor_addr,
  input  stor,
  output [7:0] stor_out
);

  wire clock_1_out;

  Clock clock_1 (.out(clock_1_out));
  RAM ram_1 (.addr(stor_addr), .we(stor), .oe(1'b1), .clk(clock_1_out), .din(stor_in), .dout(stor_out));
endmodule

module rom_instru (
  input  [23:0] addr,
  output [23:0] instru_out
);

  ROM #(.addrWidth(24), .dataWidth(24)) rom_1 (.addr(addr), .data(instru_out));
endmodule
