// Logisim project registry_file.circ as structural Verilog: 4 circuits, main circuit bits_registry
module bits_registry (
  input  [7:0] A,
  input  We,
  output [7:0] S
);

  wire and_1_out, clock_1_out;

  Clock clock_1 (.out(clock_1_out));
  and and_1 (and_1_out, clock_1_out, We);
  D_Flip_Flop d_ff_1 (.D(A[0]), .clk(and_1_out), .Q(S[0]));  // open: Qn, preset, reset
  D_Flip_Flop d_ff_2 (.D(A[1]), .clk(and_1_out), .Q(S[1]));  // open: Qn, preset, reset
  D_Flip_Flop d_ff_3 (.D(A[2]), .clk(and_1_out), .Q(S[2]));  // open: Qn, preset, reset
  D_Flip_Flop d_ff_4 (.D(A[3]), .clk(and_1_out), .Q(S[3]));  // open: Qn, preset, reset
  D_Flip_Flop d_ff_5 (.D(A[4]), .clk(and_1_out), .Q(S[4]));  // open: Qn, preset, reset
  D_Flip_Flop d_ff_6 (.D(A[5]), .clk(and_1_out), .Q(S[5]));  // open: Qn, preset, reset
  D_Flip_Flop d_ff_7 (.D(A[6]), .clk(and_1_out), .Q(S[6]));  // open: Qn, preset, reset
  D_Flip_Flop d_ff_8 (.D(A[7]), .clk(and_1_out), .Q(S[7]));  // open: Qn, preset, reset
endmodule

module bit_registry (
  input  A,
  input  We,
  output S
);

  wire and_1_out, clock_1_out;

  Clock clock_1 (.out(clock_1_out));
  and and_1 (and_1_out, clock_1_out, We);
  D_Flip_Flop d_ff_1 (.D(A), .clk(and_1_out), .Q(S));  // open: Qn, preset, reset
endmodule

module registry (
  input  [7:0] C,
  input  R0,
  input  R1,
  input  R2,
  input  R3,
  input  R4,
  input  R5,
  input  R6,
  input  R7,
  output [7:0] S0,
  output [7:0] S1,
  output [7:0] S2,
  output [7:0] S3,
  output [7:0] S4,
  output [7:0] S5,
  output [7:0] S6,
  output [7:0] S7_8bit,
  output S7_1bit
);

  bits_registry bits_registry_1 (.A(C), .We(R0), .S(S0));
  bits_registry bits_registry_2 (.A(C), .We(R1), .S(S1));
  bits_registry bits_registry_3 (.A(C), .We(R2), .S(S2));
  bits_registry bits_registry_4 (.A(C), .We(R3), .S(S3));
  bits_registry bits_registry_5 (.A(C), .We(R4), .S(S4));
  bits_registry bits_registry_6 (.A(C), .We(R5), .S(S5));
  bits_registry bits_registry_7 (.A(C), .We(R6), .S(S6));
  bit_registry bit_registry_1 (.A(C[0]), .We(R7), .S(S7_1bit));
  assign S7_8bit = {{7{1'b0}}, S7_1bit};  // Bit_Extender bit_extender_1
endmodule

module registry_24bits (
  input  [23:0] instru,
  input  We,
  output [23:0] S
);

  wire and_1_out, clock_1_out;

  Clock clock_1 (.out(clock_1_out));
  and and_1 (and_1_out, clock_1_out, We);
  bits_registry bits_registry_1 (.A(instru[7:0]), .We(and_1_out), .S(S[7:0]));
  bits_registry bits_registry_2 (.A(instru[15:8]), .We(and_1_out), .S(S[15:8]));
  bits_registry bits_registry_3 (.A(instru[23:16]), .We(and_1_out), .S(S[23:16]));
endmodule
