// Logisim project squidcpu.circ as structural Verilog: 1 circuit, main circuit main
module main (
);

  wire alu_registry_1_zero, fetch_decode_1_p2, fetch_decode_1_p5, fetch_decode_1_p7;
  wire [1:0] fetch_decode_1_p4;
  wire [3:0] fetch_decode_1_p8, fetch_decode_1_p9, fetch_decode_1_p10, fetch_decode_1_p11;
  wire [7:0] alu_registry_1_alu_out, alu_registry_1_reg_out, fetch_decode_1_p3, pc_1_addr_code,
       pc_1_addr_data, pc_1_reg_in, ram_data_1_stor_out;
  wire [23:0] rom_instru_1_instru_out;

  ram_data ram_data_1 (
    .stor_addr(pc_1_addr_data), .We(fetch_decode_1_p7), .stor_in(alu_registry_1_reg_out),
    .stor_out(ram_data_1_stor_out));
  rom_instru rom_instru_1 (.addr(pc_1_addr_code), .instru_out(rom_instru_1_instru_out));
  // fetch_decode fetch_decode_1: pin names not known; wires that end beside it: rom_instru_1_instru_out, fetch_decode_1_p2, fetch_decode_1_p3, fetch_decode_1_p4, fetch_decode_1_p5, fetch_decode_1_p5, fetch_decode_1_p7, fetch_decode_1_p8, fetch_decode_1_p9, fetch_decode_1_p10, fetch_decode_1_p11
  pc pc_1 (
    .RAM(ram_data_1_stor_out), .ALU(alu_registry_1_alu_out), .jmp(fetch_decode_1_p2),
    .addr8(fetch_decode_1_p3), .slctREG_IN(fetch_decode_1_p4), .addr_data(pc_1_addr_data),
    .REG_IN(pc_1_reg_in), .addr_code(pc_1_addr_code));
  alu_registry alu_registry_1 (
    .Rin2(fetch_decode_1_p9), .Rout(fetch_decode_1_p8), .REG_In(pc_1_reg_in), .Rin1(fetch_decode_1_p10),
    .Op(fetch_decode_1_p11), .Zero(alu_registry_1_zero), .REG_Out(alu_registry_1_reg_out),
    .ALU_Out(alu_registry_1_alu_out));
endmodule
